// Logisim project ECE150DEMO1stAttempt (1).circ as structural Verilog: 1 circuit, main circuit DLDProject1
module DLDProject1 (
  input  A,
  input  B,
  input  C,
  input  D,
  output G1,
  output R1,
  output G2,
  output R2,
  output G3,
  output R3,
  output G4,
  output R4
);

  wire AC_out, AnCnD_out, AnnD_out, BC_out, BD_out, BnCnD_out, BnD_out, CD_out, CnD_out, nAnBnCD_out,
       nAnCnD_out, nBCD_out, nBCnD_out, nBnCD_out, nCD_out, nCnD_out, not_1_out, not_2_out, not_3_out,
       not_4_out;

  not not_1 (not_1_out, A);
  not not_2 (not_2_out, B);
  not not_3 (not_3_out, C);
  not not_4 (not_4_out, D);
  and CnD (CnD_out, not_4_out, C);
  and nCD (nCD_out, not_3_out, D);
  and nCnD (nCnD_out, not_4_out, not_3_out);
  and CD (CD_out, C, D);
  and BC (BC_out, B, C);
  and BD (BD_out, B, D);
  and AC (AC_out, A, C);
  and BnD (BnD_out, B, not_4_out);
  and AnnD (AnnD_out, A, not_4_out);
  and nAnCnD (nAnCnD_out, not_1_out, nCnD_out);
  and AnCnD (AnCnD_out, A, nCnD_out);
  and BnCnD (BnCnD_out, B, nCnD_out);
  and nBCnD (nBCnD_out, not_2_out, CnD_out);
  and nBnCD (nBnCD_out, not_2_out, nCD_out);
  and BnCD (G4, nCD_out, B);
  and nBCD (nBCD_out, CD_out, not_2_out);
  and nAnBnCD (nAnBnCD_out, not_1_out, nBnCD_out);
  or R1gate (R1, A, nBCnD_out, BD_out, nCD_out);
  or G2gate (G2, nBCD_out, AnCnD_out, G4);
  or R2gate (R2, AC_out, nBnCD_out, BC_out, BnD_out);
  or G3gate (G3, BC_out, BD_out, CD_out);
  or R3gate (R3, nAnBnCD_out, AnnD_out, BnCnD_out);
  or R4gate (R4, nAnBnCD_out, AnCnD_out, BC_out, BnD_out);
  or G1gate (G1, nAnCnD_out, nBCD_out, BnD_out);
endmodule
