// Logisim project NANDSimulation.circ as structural Verilog: 1 circuit, main circuit main
module main (
  input  A,
  input  B,
  input  C,
  input  D
);

  wire Aa_out, BD_out, BnD_out, G1_out, nA_out, nAnCnD_out, nand_1_out, nand_2_out, nand_3_out, nand_4_out,
       nand_5_out, nand_6_out, nand_7_out, nand_8_out, nand_9_out, nand_10_out, nand_11_out, nand_12_out,
       nand_13_out, nand_14_out, nand_15_out, nand_16_out, nand_17_out, nand_18_out, nB_out, nBCD_out,
       nBCnD_out, nC_out, nCD_out, nD_out, R1_out;

  nand nA (nA_out, A, A);
  nand nB (nB_out, B, B);
  nand nC (nC_out, C, C);
  nand nD (nD_out, D, D);
  nand nand_1 (nand_1_out, nA_out, nC_out);
  nand nand_2 (nand_2_out, nB_out, C);
  nand nand_3 (nand_3_out, nB_out, C);
  nand nand_4 (nand_4_out, nand_1_out, nand_1_out);
  nand nand_5 (nand_5_out, nand_2_out, nand_2_out);
  nand nand_6 (nand_6_out, nand_3_out, nand_3_out);
  nand nand_7 (nand_7_out, B, D);
  nand nand_8 (nand_8_out, nand_4_out, nD_out);
  nand nand_9 (nand_9_out, nand_5_out, D);
  nand nand_10 (nand_10_out, nD_out, B);
  nand nand_11 (nand_11_out, nand_6_out, nD_out);
  nand nand_12 (nand_12_out, D, nC_out);
  nand nAnCnD (nAnCnD_out, nand_8_out, nand_8_out);
  nand nBCD (nBCD_out, nand_9_out, nand_9_out);
  nand BnD (BnD_out, nand_10_out, nand_10_out);
  nand BD (BD_out, nand_7_out, nand_7_out);
  nand nCD (nCD_out, nand_12_out, nand_12_out);
  nand nBCnD (nBCnD_out, nand_11_out, nand_11_out);
  nand nand_13 (nand_13_out, nAnCnD_out, nAnCnD_out);
  nand nand_14 (nand_14_out, nBCD_out, nBCD_out);
  nand nand_15 (nand_15_out, BnD_out, BnD_out);
  nand Aa (Aa_out, A, A);
  nand nand_16 (nand_16_out, nBCnD_out, nBCnD_out);
  nand nand_17 (nand_17_out, BD_out, BD_out);
  nand nand_18 (nand_18_out, nCD_out, nCD_out);
  nand G1 (G1_out, nand_13_out, nand_14_out, nand_15_out);
  nand R1 (R1_out, Aa_out, nand_16_out, nand_17_out, nand_18_out);
  // RGBLED RGB1: pin names not known; wires that end beside it: R1_out, R1_out, G1_out
endmodule
